# Fritzing sketch lighthouse-leds-1 (saved by Fritzing 1.0.1rc)
breadboards: 1

parts:
  Pico_H1 = Raspberry Pi Pico H
  R1 = Resistor [tolerance=±5% power=0.25W resistance=1k package=THT]
  Schiermonnikoog = smd LED [color="White (6500K)" package="0805 [SMD]"]
  R2 = Resistor [tolerance=±5% power=0.25W resistance=1k package=THT]
  Ameland = smd LED [color="White (6500K)" package="0805 [SMD]"]
  Terschelling = smd LED [color="White (6500K)" package="0805 [SMD]"]
  Vlieland = smd LED [color="White (6500K)" package="0805 [SMD]"]
  Texel = smd LED [color="White (6500K)" package="0805 [SMD]"]
  R3 = Resistor [tolerance=±5% power=0.25W resistance=1k package=THT]
  R4 = Resistor [tolerance=±5% power=0.25W resistance=1k package=THT]
  R6 = Resistor [tolerance=±5% power=0.25W resistance=1k package=THT]
  R7 = Resistor [tolerance=±5% power=0.25W resistance=1k package=THT]
  LED3 = smd LED [color="Green (565nm)" package="0805 [SMD]"]
  LED2 = smd LED [color="Red (633nm)" package="0805 [SMD]"]
  use_this_resistor_to_bypass_night/day_cycle_remove_otherwise = Resistor [tolerance=±5% power=0.25W resistance=1k package=THT]

nets:
  N1: Pico_H1.VSYS, LED2.anode
  N2: Pico_H1.GND, Schiermonnikoog.cathode, Ameland.cathode, Terschelling.cathode, Vlieland.cathode, Texel.cathode, LED3.cathode, use_this_resistor_to_bypass_night/day_cycle_remove_otherwise.Pin_0
  N3: Pico_H1.GP20, R1.Pin_1
  N4: Pico_H1.GP19, R2.Pin_1
  N5: Pico_H1.GP18, R6.Pin_1
  N6: Pico_H1.GP17, R3.Pin_1
  N7: Pico_H1.GP16, R4.Pin_1
  N8: Pico_H1.GP2, use_this_resistor_to_bypass_night/day_cycle_remove_otherwise.Pin_1
  N9: R1.Pin_0, Schiermonnikoog.anode
  N10: R2.Pin_0, Ameland.anode
  N11: Terschelling.anode, R6.Pin_0
  N12: Vlieland.anode, R3.Pin_0
  N13: Texel.anode, R4.Pin_0
  N14: R7.Pin_0, LED3.anode
  N15: R7.Pin_1, LED2.cathode

custom parts:
  Raspberry Pi Pico H: Raspberry Pi Pico H. Based around the RP2040 microcontroller the Pico H is a low cost microcontroller device bringing Raspberry Pi quality, cost, and easy of use to the microcontroller space.
